// Logisim project ddco_assign.circ as structural Verilog: 1 circuit, main circuit main
module main (
  input  least_significant,
  input  in_2,
  input  in_3,
  input  in_4,
  input  in_5,
  input  in_6,
  input  MSB
);

  wire a_out, a_prime_b_2_out, a_prime_b_out, a_prime_b_prime_out, a_prime_c_prime_out, ab__prime_out,
       ab_prime_c_out, adder_1_cout, adder_1_out, adder_2_cout, adder_2_out, adder_3_cout, adder_3_out,
       adder_4_cout, adder_4_out, b_a_out, b_c_prime_out, b_out, bc_prime_out, c_a_out, c_ab__prime_out,
       c_b_out, c_out, d_out, e_out, f_out, g_out;

  Adder #(.width(1)) adder_1 (.a(in_3), .b(in_4), .out(adder_1_out), .cin(in_2), .cout(adder_1_cout));
  Adder #(.width(1)) adder_2 (.a(in_6), .b(MSB), .out(adder_2_out), .cin(in_5), .cout(adder_2_cout));
  Adder #(.width(1)) adder_3 (
    .a(adder_1_out), .b(adder_2_out), .out(adder_3_out), .cin(least_significant), .cout(adder_3_cout));
  Adder #(.width(1)) adder_4 (
    .a(adder_1_cout), .b(adder_2_cout), .out(adder_4_out), .cin(adder_3_cout), .cout(adder_4_cout));
  nand ab__prime (ab__prime_out, adder_3_out, adder_4_out);
  and a_prime_b_prime (a_prime_b_prime_out, ~adder_4_out, ~adder_3_out);  // AND_Gate
  and c_ab__prime (c_ab__prime_out, adder_4_cout, ab__prime_out);
  and bc_prime (bc_prime_out, adder_4_out, ~adder_4_cout);  // AND_Gate
  and a_prime_c_prime (a_prime_c_prime_out, ~adder_4_cout, ~adder_3_out);  // AND_Gate
  xnor b_a (b_a_out, adder_4_out, adder_3_out);
  xnor c_a (c_a_out, adder_4_cout, adder_3_out);
  and a_prime_b (a_prime_b_out, ~adder_3_out, adder_4_out);  // AND_Gate
  xor c_b (c_b_out, adder_4_cout, adder_4_out);
  or b_c_prime (b_c_prime_out, adder_4_out, ~adder_4_cout);  // OR_Gate
  and ab_prime_c (ab_prime_c_out, adder_3_out, ~adder_4_out, adder_4_cout);  // AND_Gate
  and a_prime_b_2 (a_prime_b_2_out, ~adder_3_out, adder_4_out);  // AND_Gate
  or b (b_out, b_a_out, ~adder_4_cout);  // OR_Gate
  or a (a_out, c_a_out, adder_4_out);
  or f (f_out, a_prime_b_prime_out, c_ab__prime_out);
  or g (g_out, a_prime_b_out, c_b_out);
  and e (e_out, ~adder_3_out, b_c_prime_out);  // AND_Gate
  or d (d_out, bc_prime_out, a_prime_b_2_out, ab_prime_c_out, a_prime_c_prime_out);
  or c (c_out, adder_3_out, ~adder_4_out, adder_4_cout);  // OR_Gate
  _7_Segment_Display u_7_segment_display_1 (
    .g(g_out), .f(f_out), .a(a_out), .b(b_out), .e(e_out), .d(d_out), .c(c_out));  // open: dp

  // Notes on the sheet:
  //   a
  //   b
  //   c
endmodule
